// Logisim project mips_processor.circ as structural Verilog: 10 circuits, main circuit MIPS
module MIPS (
  input  clear,
  input  clear_2
);

  wire clk;
  wire [4:0] if_id_1_rs, if_id_1_rt;
  wire [5:0] if_id_1_opcode;
  wire [31:0] imem_1_instruction, imem_1_pc, regfile_1_readdata1, regfile_1_readdata2;

  Clock clock_1 (.out(clk));
  IMEM imem_1 (.CLK(clk), .PC(imem_1_pc), .INSTRUCTION(imem_1_instruction));  // open: BranchAddress, PCSRC
  IF_ID if_id_1 (
    .INSTRUCTION(imem_1_instruction), .PC(imem_1_pc), .CLEAR(clear_2), .CLK(clk), .OPCODE(if_id_1_opcode),
    .RS(if_id_1_rs), .RT(if_id_1_rt));  // open: RD, SHAMT, FUNCT, IMMEDIATE, ADDRESS, PC_2
  CONTROL control_1 (.OpCode(if_id_1_opcode));  // open: ALUOp, Branch, RegWrite, MemRead, MemtoReg, RegDst, ALUSrc, MemWrite
  REGFILE regfile_1 (
    .readR1(if_id_1_rs), .readR2(if_id_1_rt), .clk(clk), .ReadData1(regfile_1_readdata1),
    .ReadData2(regfile_1_readdata2));  // open: RegWrite, RegWriteAddress, WriteData
  ID_EX id_ex_1 (
    .ReadData1(regfile_1_readdata1), .ReadData2(regfile_1_readdata2), .CLEAR(clear), .CLK(clk));  // open: PC, RegWrite, MemToReg, MemWrite, MemRead, Branch, AluOp, RegDst, AluSrc, Immediate, RT, RD, ENABLE, PC_2, RegWrite_2, MemToReg_2, MemWrite_2, MemRead_2, Branch_2, AluOp_2, RegDst_2, AluSrc_2, ReadData1_2, ReadData2_2, IMMEADIATE, RT_2, RD_2
  ALU alu_1 ();  // open: R1, R2, Funct, ALUOp, B_Out, Output_Reg, Zero, C_Out
  EX_MEM ex_mem_1 (.CLK(clk));  // open: BranchAddress, ADD_Result, ALU_Zero, ALU_Result, Write_reg, WB, MEM, CLEAR, Branch_Address, Add_Result_Output, ZERO, ALU_Result_Output, Write_Reg_2, WB_2, MEM_2
  DMEM dmem_1 (.CLK(clk));  // open: Address, Data, MemWrite, MemRead, Output
  MEM_WB mem_wb_1 (.CLK(clk));  // open: Write_reg, Read_Data, ALU_Result, WB, Write_reg_2, Read_Data_Output, ALU_Result_Output, WB_2
endmodule

module ALU (
  input  [31:0] R1,
  input  [31:0] R2,
  input  [5:0] Funct,
  input  [1:0] ALUOp,
  output [31:0] Output_Reg,
  output Zero,
  output C_Out,
  output B_Out
);

  wire comparator_1_lt, or_2_out;
  wire [3:0] ALU_Control, R_Format;
  wire [31:0] adder_1_out, and_1_out, bit_extender_1_out, or_1_out, signal;

  assign and_1_out = R1 & R1;  // AND_Gate and_1, 32 bits wide
  assign or_1_out = R1 | R1;  // OR_Gate or_1, 32 bits wide
  Adder #(.width(32)) adder_1 (.a(R1), .b(R2), .out(adder_1_out), .cin(1'b0), .cout(C_Out));
  Subtractor #(.width(32)) subtractor_1 (.a(R1), .b(R2), .out(signal), .bin(1'b0), .bout(B_Out));
  Comparator #(.width(32)) comparator_1 (.a(R1), .b(R2), .lt(comparator_1_lt));  // open: gt, eq
  Multiplexer #(.select(4), .width(4), .disabled(0)) multiplexer_1 (
    .in0(4'b0010), .in1(4'b0110), .in4(4'b0000), .in5(4'b0001), .in10(4'b0111), .out(R_Format),
    .sel(Funct[3:0]), .en(1'b1));  // open: in2, in3, in6, in7, in8, in9, in11, in12, in13, in14, in15
  assign bit_extender_1_out = {{31{1'b0}}, comparator_1_lt};  // Bit_Extender bit_extender_1
  Multiplexer #(.select(4), .width(32), .disabled(0)) multiplexer_2 (
    .in0(and_1_out), .in1(or_1_out), .in2(adder_1_out), .in6(signal), .in7(bit_extender_1_out),
    .out(Output_Reg), .sel(ALU_Control), .en(1'b1));  // open: in3, in4, in5, in8, in9, in10, in11, in12, in13, in14, in15
  Multiplexer #(.select(2), .width(4), .disabled(0)) multiplexer_3 (
    .in0(4'b0010), .in1(4'b0110), .in2(R_Format), .out(ALU_Control), .sel(ALUOp), .en(1'b1));  // open: in3
  or or_2 (or_2_out, signal[0], signal[1], signal[2], signal[3], signal[4], signal[5], signal[6], signal[7], signal[8], signal[9], signal[10], signal[11], signal[12], signal[13], signal[14], signal[15], signal[17], signal[18], signal[19], signal[20], signal[21], signal[22], signal[23], signal[24], signal[25], signal[26], signal[27], signal[28], signal[29], signal[30], signal[31], signal[16]);
  not not_1 (Zero, or_2_out);

  // Notes on the sheet:
  //   AND
  //   OR
  //   ADD
  //   Subtract
  //   Set less than
endmodule

module IMEM (
  input  [31:0] BranchAddress,
  input  PCSRC,
  input  CLK,
  output [31:0] PC,
  output [31:0] INSTRUCTION
);

  wire not_1_out, not_2_out, not_3_out, not_4_out, not_5_out, not_6_out, not_7_out, not_8_out, not_9_out;
  wire [31:0] adder_1_out, multiplexer_1_out, ram_1_data, ram_2_data, ram_3_data, ram_4_data;

  Multiplexer #(.width(32)) multiplexer_1 (
    .in0(adder_1_out), .in1(BranchAddress), .out(multiplexer_1_out), .sel(PCSRC), .en(1'b1));
  not not_1 (not_1_out, 1'b0);
  not not_2 (not_2_out, 1'b0);
  not not_3 (not_3_out, 1'b0);
  not not_4 (not_4_out, 1'b0);
  not not_5 (not_5_out, 1'b0);
  not not_6 (not_6_out, 1'b0);
  not not_7 (not_7_out, 1'b0);
  not not_8 (not_8_out, 1'b0);
  not not_9 (not_9_out, 1'b0);
  Register #(.width(32)) u_PC (.D(multiplexer_1_out), .en(not_1_out), .Q(PC), .clk(CLK), .clr(1'b0));
  RAM #(.addrWidth(24), .dataWidth(32)) ram_1 (
    .addr(PC[25:2]), .data(ram_1_data), .sel(not_2_out), .clk(CLK), .ld(not_3_out), .clr(1'b0));
  RAM #(.addrWidth(24), .dataWidth(32)) ram_2 (
    .addr(PC[25:2]), .data(ram_2_data), .sel(not_4_out), .clk(CLK), .ld(not_5_out), .clr(1'b0));
  RAM #(.addrWidth(24), .dataWidth(32)) ram_3 (
    .addr(PC[25:2]), .data(ram_3_data), .sel(not_7_out), .clk(CLK), .ld(not_6_out), .clr(1'b0));
  RAM #(.addrWidth(24), .dataWidth(32)) ram_4 (
    .addr(PC[25:2]), .data(ram_4_data), .sel(not_9_out), .clk(CLK), .ld(not_8_out), .clr(1'b0));
  Adder #(.width(32)) adder_1 (.a(32'h4), .b(PC), .out(adder_1_out), .cin(1'b0));  // open: cout
  Multiplexer #(.select(2), .width(32)) multiplexer_2 (
    .in0(ram_1_data), .in1(ram_2_data), .in2(ram_3_data), .in3(ram_4_data), .out(INSTRUCTION),
    .sel(PC[27:26]), .en(1'b1));
endmodule

module DMEM (
  input  [23:0] Address,
  input  [31:0] Data,
  input  CLK,
  input  MemRead,
  input  MemWrite,
  output [31:0] Output
);

  wire not_1_out;

  not not_1 (not_1_out, 1'b0);
  RAM #(.addrWidth(24), .dataWidth(32), .bus("separate")) ram_1 (
    .addr(Address), .din(Data), .data(Output), .str(MemWrite), .sel(not_1_out), .clk(CLK), .ld(MemRead),
    .clr(1'b0));
endmodule

module REGFILE (
  input  [4:0] readR1,
  input  [4:0] readR2,
  input  RegWrite,
  input  clk,
  input  [4:0] RegWriteAddress,
  input  [31:0] WriteData,
  output [31:0] ReadData1,
  output [31:0] ReadData2
);

  wire Wa0, Wa1, Wa2, Wa3, Wat, Wfp, Wgp, Wk0, Wk1, Wra, Ws0, Ws1, Ws2, Ws3, Ws4, Ws5, Ws6, Ws7, Wsp, Wt0,
       Wt1, Wt2, Wt3, Wt4, Wt5, Wt6, Wt7, Wt8, Wt9, Wv0, Wv1, WZero;
  wire [4:0] readRegister1_q, readRegister2_q;
  wire [31:0] a0, a1, a2, a3, at, fp, gp, k0, k1, ra, s0, s1, s2, s3, s4, s5, s6, s7, sp, t0, t1, t2, t3, t4,
       t5, t6, t7, t8, t9, v0, v1, Write_to_Register, Zero;

  Decoder #(.select(5), .disabled(0)) decoder_1 (
    .out0(WZero), .out1(Wat), .out2(Wv0), .out3(Wv1), .out4(Wa0), .out5(Wa1), .out6(Wa2), .out7(Wa3),
    .out8(Wt0), .out9(Wt1), .out10(Wt2), .out11(Wt3), .out12(Wt4), .out13(Wt5), .out14(Wt6), .out15(Wt7),
    .out16(Ws0), .out17(Ws1), .out18(Ws2), .out19(Ws3), .out20(Ws4), .out21(Ws5), .out22(Ws6), .out23(Ws7),
    .out24(Wt8), .out25(Wt9), .out26(Wk0), .out27(Wk1), .out28(Wgp), .out29(Wsp), .out30(Wfp), .out31(Wra),
    .sel(RegWriteAddress), .en(RegWrite));
  Register #(.width(5)) readRegister2 (.D(readR2), .en(1'b1), .Q(readRegister2_q), .clk(clk), .clr(1'b0));
  Multiplexer #(.select(5), .width(32), .enable("false")) multiplexer_1 (
    .in0(Zero), .in1(at), .in2(v0), .in3(v1), .in4(a0), .in5(a1), .in6(a2), .in7(a3), .in8(t0), .in9(t1),
    .in10(t2), .in11(t3), .in12(t4), .in13(t5), .in14(t6), .in15(t7), .in16(s0), .in17(s1), .in18(s2),
    .in19(s3), .in20(s4), .in21(s5), .in22(s6), .in23(s7), .in24(t8), .in25(t9), .in26(k0), .in27(k1),
    .in28(gp), .in29(sp), .in30(fp), .in31(ra), .out(ReadData1), .sel(readRegister1_q));
  Multiplexer #(.select(5), .width(32), .enable("false")) multiplexer_2 (
    .in0(Zero), .in1(at), .in2(v0), .in3(v1), .in4(a0), .in5(a1), .in6(a2), .in7(a3), .in8(t0), .in9(t1),
    .in10(t2), .in11(t3), .in12(t4), .in13(t5), .in14(t6), .in15(t7), .in16(s0), .in17(s1), .in18(s2),
    .in19(s3), .in20(s4), .in21(s5), .in22(s6), .in23(s7), .in24(t8), .in25(t9), .in26(k0), .in27(k1),
    .in28(gp), .in29(sp), .in30(fp), .in31(ra), .out(ReadData2), .sel(readRegister2_q));
  Register #(.width(5)) readRegister1 (.D(readR1), .en(1'b1), .Q(readRegister1_q), .clk(clk), .clr(1'b0));
  Register #(.width(32)) u_writedata (.D(WriteData), .en(1'b1), .Q(Write_to_Register), .clk(clk), .clr(1'b0));
  Register #(.width(32)) register_1 (.D(Write_to_Register), .en(Wv0), .Q(v0), .clk(clk), .clr(1'b0));
  Register #(.width(32)) register_2 (.D(Write_to_Register), .en(Wv1), .Q(v1), .clk(clk), .clr(1'b0));
  Register #(.width(32)) register_3 (.D(Write_to_Register), .en(WZero), .Q(Zero), .clk(clk), .clr(1'b0));
  Register #(.width(32)) register_4 (.D(Write_to_Register), .en(Wa0), .Q(a0), .clk(clk), .clr(1'b0));
  Register #(.width(32)) register_5 (.D(Write_to_Register), .en(Wa1), .Q(a1), .clk(clk), .clr(1'b0));
  Register #(.width(32)) register_6 (.D(Write_to_Register), .en(Wa2), .Q(a2), .clk(clk), .clr(1'b0));
  Register #(.width(32)) register_7 (.D(Write_to_Register), .en(Wa3), .Q(a3), .clk(clk), .clr(1'b0));
  Register #(.width(32)) register_8 (.D(Write_to_Register), .en(Wt0), .Q(t0), .clk(clk), .clr(1'b0));
  Register #(.width(32)) register_9 (.D(Write_to_Register), .en(Wt1), .Q(t1), .clk(clk), .clr(1'b0));
  Register #(.width(32)) register_10 (.D(Write_to_Register), .en(Wt2), .Q(t2), .clk(clk), .clr(1'b0));
  Register #(.width(32)) register_11 (.D(Write_to_Register), .en(Wt8), .Q(t8), .clk(clk), .clr(1'b0));
  Register #(.width(32)) register_12 (.D(Write_to_Register), .en(Wt9), .Q(t9), .clk(clk), .clr(1'b0));
  Register #(.width(32)) register_13 (.D(Write_to_Register), .en(Wk0), .Q(k0), .clk(clk), .clr(1'b0));
  Register #(.width(32)) register_14 (.D(Write_to_Register), .en(Wk1), .Q(k1), .clk(clk), .clr(1'b0));
  Register #(.width(32)) register_15 (.D(Write_to_Register), .en(Wgp), .Q(gp), .clk(clk), .clr(1'b0));
  Register #(.width(32)) register_16 (.D(Write_to_Register), .en(Wfp), .Q(fp), .clk(clk), .clr(1'b0));
  Register #(.width(32)) register_17 (.D(Write_to_Register), .en(Wat), .Q(at), .clk(clk), .clr(1'b0));
  Register #(.width(32)) register_18 (.D(Write_to_Register), .en(Ws0), .Q(s0), .clk(clk), .clr(1'b0));
  Register #(.width(32)) register_19 (.D(Write_to_Register), .en(Ws1), .Q(s1), .clk(clk), .clr(1'b0));
  Register #(.width(32)) register_20 (.D(Write_to_Register), .en(Ws2), .Q(s2), .clk(clk), .clr(1'b0));
  Register #(.width(32)) register_21 (.D(Write_to_Register), .en(Wt7), .Q(t7), .clk(clk), .clr(1'b0));
  Register #(.width(32)) register_22 (.D(Write_to_Register), .en(Wt6), .Q(t6), .clk(clk), .clr(1'b0));
  Register #(.width(32)) register_23 (.D(Write_to_Register), .en(Wt5), .Q(t5), .clk(clk), .clr(1'b0));
  Register #(.width(32)) register_24 (.D(Write_to_Register), .en(Wt4), .Q(t4), .clk(clk), .clr(1'b0));
  Register #(.width(32)) register_25 (.D(Write_to_Register), .en(Wt3), .Q(t3), .clk(clk), .clr(1'b0));
  Register #(.width(32)) register_26 (.D(Write_to_Register), .en(Ws3), .Q(s3), .clk(clk), .clr(1'b0));
  Register #(.width(32)) register_27 (.D(Write_to_Register), .en(Ws4), .Q(s4), .clk(clk), .clr(1'b0));
  Register #(.width(32)) register_28 (.D(Write_to_Register), .en(Ws5), .Q(s5), .clk(clk), .clr(1'b0));
  Register #(.width(32)) register_29 (.D(Write_to_Register), .en(Ws6), .Q(s6), .clk(clk), .clr(1'b0));
  Register #(.width(32)) register_30 (.D(Write_to_Register), .en(Wra), .Q(ra), .clk(clk), .clr(1'b0));
  Register #(.width(32)) register_31 (.D(Write_to_Register), .en(Ws7), .Q(s7), .clk(clk), .clr(1'b0));
  Register #(.width(32)) register_32 (.D(Write_to_Register), .en(Wsp), .Q(sp), .clk(clk), .clr(1'b0));
endmodule

module CONTROL (
  input  [5:0] OpCode,
  output [1:0] ALUOp,
  output Branch,
  output RegWrite,
  output MemRead,
  output MemtoReg,
  output RegDst,
  output ALUSrc,
  output MemWrite
);

  wire j, not_1_out, not_3_out, not_4_out;

  Decoder #(.select(5), .disabled(0)) decoder_1 (
    .out0(ALUOp[1]), .out2(j), .out4(ALUOp[0]), .out23(MemRead), .sel(OpCode[4:0]), .en(not_1_out));  // open: out1, out3, out5, out6, out7, out8, out9, out10, out11, out12, out13, out14, out15, out16, out17, out18, out19, out20, out21, out22, out24, out25, out26, out27, out28, out29, out30, out31
  not not_1 (not_1_out, OpCode[5]);
  Decoder #(.select(5), .disabled(0)) decoder_2 (
    .out11(MemWrite), .sel(OpCode[4:0]), .en(OpCode[5]));  // open: out0, out1, out2, out3, out4, out5, out6, out7, out8, out9, out10, out12, out13, out14, out15, out16, out17, out18, out19, out20, out21, out22, out23, out24, out25, out26, out27, out28, out29, out30, out31
  not not_2 (MemtoReg, MemRead);
  not not_3 (not_3_out, ALUOp[0]);
  not not_4 (not_4_out, ALUOp[1]);
  or or_1 (RegWrite, ALUOp[1], MemRead);
  or or_2 (ALUSrc, not_3_out, MemRead, not_4_out, MemWrite);

  assign Branch = ALUOp[0];
  assign RegDst = ALUOp[1];

  // Other names for the same wires on the sheet: beq = ALUOp[0]; R = ALUOp[1]; lw = MemRead;
  //   Op_Code[4:0] = OpCode[4:0]; Op_Code_1 = OpCode[5]; sw = MemWrite
endmodule

module IF_ID (
  input  CLEAR,
  input  [31:0] INSTRUCTION,
  input  [31:0] PC,
  input  CLK,
  output [5:0] OPCODE,
  output [4:0] RS,
  output [4:0] RT,
  output [4:0] RD,
  output [4:0] SHAMT,
  output [5:0] FUNCT,
  output [15:0] IMMEDIATE,
  output [25:0] ADDRESS,
  output [31:0] PC_2
);

  wire not_1_out;

  Register #(.width(32)) u_instruction (
    .D(INSTRUCTION), .en(1'b1), .Q({OPCODE, ADDRESS}), .clk(not_1_out), .clr(CLEAR));
  Register #(.width(32)) program_counter (.D(PC), .en(1'b1), .Q(PC_2), .clk(not_1_out), .clr(CLEAR));
  not not_1 (not_1_out, CLK);

  assign FUNCT = ADDRESS[5:0];
  assign IMMEDIATE = ADDRESS[15:0];
  assign RD = ADDRESS[15:11];
  assign RS = ADDRESS[25:21];
  assign RT = ADDRESS[20:16];
  assign SHAMT = ADDRESS[10:6];
endmodule

module ID_EX (
  input  CLEAR,
  input  [31:0] PC,
  input  RegWrite,
  input  MemToReg,
  input  MemWrite,
  input  MemRead,
  input  Branch,
  input  [1:0] AluOp,
  input  RegDst,
  input  AluSrc,
  input  [31:0] ReadData1,
  input  [31:0] ReadData2,
  input  [31:0] Immediate,
  input  [4:0] RT,
  input  [4:0] RD,
  input  ENABLE,
  input  CLK,
  output [31:0] PC_2,
  output RegWrite_2,
  output MemToReg_2,
  output MemWrite_2,
  output MemRead_2,
  output Branch_2,
  output [1:0] AluOp_2,
  output RegDst_2,
  output AluSrc_2,
  output [31:0] ReadData1_2,
  output [31:0] ReadData2_2,
  output [31:0] IMMEADIATE,
  output [4:0] RT_2,
  output [4:0] RD_2
);

  wire not_1_out;

  not not_1 (not_1_out, CLK);
  Register #(.width(32)) program_counter (.D(PC), .en(ENABLE), .Q(PC_2), .clk(not_1_out), .clr(CLEAR));
  Register #(.width(2)) wb (
    .D({RegWrite, MemToReg}), .en(ENABLE), .Q({RegWrite_2, MemToReg_2}), .clk(not_1_out), .clr(CLEAR));
  Register #(.width(3)) mem (
    .D({MemWrite, MemRead, Branch}), .en(ENABLE), .Q({MemWrite_2, MemRead_2, Branch_2}), .clk(not_1_out),
    .clr(CLEAR));
  Register #(.width(4)) ex (
    .D({AluOp, RegDst, AluSrc}), .en(ENABLE), .Q({AluOp_2, RegDst_2, AluSrc_2}), .clk(not_1_out), .clr(CLEAR));
  Register #(.width(32)) read_data1 (.D(ReadData1), .en(ENABLE), .Q(ReadData1_2), .clk(not_1_out), .clr(CLEAR));
  Register #(.width(32)) read_data2 (.D(ReadData2), .en(ENABLE), .Q(ReadData2_2), .clk(not_1_out), .clr(CLEAR));
  Register #(.width(32)) u_immediate (.D(Immediate), .en(ENABLE), .Q(IMMEADIATE), .clk(not_1_out), .clr(CLEAR));
  Register #(.width(5)) u_rt (.D(RT), .en(ENABLE), .Q(RT_2), .clk(not_1_out), .clr(CLEAR));
  Register #(.width(5)) u_rd (.D(RD), .en(ENABLE), .Q(RD_2), .clk(not_1_out), .clr(CLEAR));
endmodule

module EX_MEM (
  input  CLEAR,
  input  [31:0] BranchAddress,
  input  [31:0] ADD_Result,
  input  ALU_Zero,
  input  [31:0] ALU_Result,
  input  [4:0] Write_reg,
  input  [1:0] WB,
  input  [2:0] MEM,
  input  CLK,
  output [31:0] Branch_Address,
  output [31:0] Add_Result_Output,
  output ZERO,
  output [31:0] ALU_Result_Output,
  output [4:0] Write_Reg_2,
  output [1:0] WB_2,
  output [2:0] MEM_2
);

  wire not_1_out;

  Register #(.width(32)) program_counter (
    .D(BranchAddress), .Q(Branch_Address), .clk(not_1_out), .clr(CLEAR));  // open: en
  Register #(.width(5)) WriteReg (.D(Write_reg), .Q(Write_Reg_2), .clk(not_1_out), .clr(CLEAR));  // open: en
  Register #(.width(32)) u_ADD_Result (
    .D(ADD_Result), .Q(Add_Result_Output), .clk(not_1_out), .clr(CLEAR));  // open: en
  Register #(.width(1)) u_ALU_Zero (.D(ALU_Zero), .Q(ZERO), .clk(not_1_out), .clr(CLEAR));  // open: en
  Register #(.width(32)) u_ALU_Result (
    .D(ALU_Result), .Q(ALU_Result_Output), .clk(not_1_out), .clr(CLEAR));  // open: en
  Register #(.width(2)) u_WB (.D(WB), .Q(WB_2), .clk(not_1_out), .clr(CLEAR));  // open: en
  Register #(.width(3)) u_MEM (.D(MEM), .Q(MEM_2), .clk(not_1_out), .clr(CLEAR));  // open: en
  not not_1 (not_1_out, CLK);
endmodule

module MEM_WB (
  input  [4:0] Write_reg,
  input  [31:0] Read_Data,
  input  [31:0] ALU_Result,
  input  [1:0] WB,
  input  CLK,
  output [4:0] Write_reg_2,
  output [31:0] Read_Data_Output,
  output [31:0] ALU_Result_Output,
  output [1:0] WB_2
);

  Register #(.width(32)) Mem_Read (.D(ALU_Result), .en(1'b1), .Q(ALU_Result_Output), .clk(CLK), .clr(1'b0));
  Register #(.width(2)) Mem_Read_2 (.D(WB), .en(1'b1), .Q(WB_2), .clk(CLK), .clr(1'b0));
  Register #(.width(32)) u_Read_Data (.D(Read_Data), .en(1'b1), .Q(Read_Data_Output), .clk(CLK), .clr(1'b0));
  Register #(.width(5)) Read_Data_2 (.D(Write_reg), .en(1'b1), .Q(Write_reg_2), .clk(CLK), .clr(1'b0));
endmodule
